# Fritzing sketch XLSdoppio (saved by Fritzing 0.9.3b)
circuit board: 5cm x 1.46841cm

parts:
  J45 = female pin header, 1 pin [form="♀ (female)"]
  J46 = female pin header, 1 pin [form="♀ (female)"]
  J47 = female pin header, 1 pin [form="♀ (female)"]
  R1 = Resistor [tolerance=±5% resistance=220 package=THT]
  J48 = female pin header, 4 pins [form="♀ (female)"]
  J49 = female pin header, 1 pin [form="♀ (female)"]
  J50 = female pin header, 1 pin [form="♀ (female)"]
  J51 = female pin header, 1 pin [form="♀ (female)"]
  R2 = Resistor [tolerance=±5% resistance=220 package=THT]

nets:
  N1: J45.pin1, R1.Pin_0, J48.pin1, J51.pin1, R2.Pin_0
  N2: J46.pin1, R1.Pin_1, J48.pin4
  N3: J47.pin1, J48.pin2, J49.pin1
  N4: J48.pin3, J50.pin1, R2.Pin_1

notes:
  GND
  3V3
  Vin
  Clk
  MISO
  MOSI
  CS
  VBEN
  IRQ
