# Fritzing sketch XLStriplo (saved by Fritzing 0.9.3b)
circuit board: 8.11109cm x 1.72687cm

parts:
  R1 = Resistor [tolerance=±5% resistance=220 package=THT]
  R2 = Resistor [tolerance=±5% resistance=220 package=THT]
  R3 = Resistor [tolerance=±5% resistance=220 package=THT]
  J48 = female pin header, 5 pins [form="♀ (female)"]
  J45 = longpad pin header, 1 pin [form="long pad"]
  J47 = longpad pin header, 1 pin [form="long pad"]
  J46 = longpad pin header, 1 pin [form="long pad"]
  J50 = longpad pin header, 1 pin [form="long pad"]
  J49 = longpad pin header, 1 pin [form="long pad"]
  J51 = longpad pin header, 1 pin [form="long pad"]
  J52 = longpad pin header, 1 pin [form="long pad"]
  J53 = longpad pin header, 1 pin [form="long pad"]
  J54 = longpad pin header, 1 pin [form="long pad"]

nets:
  N1: R1.Pin_0, R2.Pin_0, R3.Pin_0, J48.pin1, J45.pin1, J51.pin1, J54.pin1
  N2: R1.Pin_1, J48.pin5, J46.pin1
  N3: R2.Pin_1, J48.pin4, J50.pin1
  N4: R3.Pin_1, J48.pin3, J53.pin1
  N5: J48.pin2, J47.pin1, J49.pin1, J52.pin1

notes:
  GND
  3V3
  Vin
  Clk
  MISO
  MOSI
  CS
  VBEN
  IRQ
