# Fritzing sketch Arduino-Board Bridge 2 (saved by Fritzing 0.9.3b)
circuit board: 3.74147cm x 1.22157cm
breadboards: 1

parts:
  J2 = female pin header, 8 pins [form="♀ (female)"]
  J3 = female pin header, 8 pins [form="♀ (female)"]
  J1 = female pin header, 5 pins [form="♀ (female)"]
  J4 = female pin header, 5 pins [form="♀ (female)"]

nets:
  N1: J2.pin1, J3.pin1
  N2: J2.pin2, J3.pin2
  N3: J2.pin3, J3.pin3
  N4: J2.pin4, J3.pin4
  N5: J2.pin5, J3.pin5
  N6: J2.pin6, J3.pin6
  N7: J2.pin7, J3.pin7
  N8: J2.pin8, J3.pin8
  N9: J1.pin1, J4.pin1
  N10: J1.pin2, J4.pin2
  N11: J1.pin3, J4.pin3
  N12: J1.pin4, J4.pin4
  N13: J1.pin5, J4.pin5
