# Fritzing sketch Bridges_XLS (saved by Fritzing 0.9.3b)
circuit board: 15cm x 10cm
breadboards: 1

parts:
  J5 = female pin header, 8 pins [form="♀ (female)"]
  J6 = female pin header, 8 pins [form="♀ (female)"]
  J7 = female pin header, 8 pins [form="♀ (female)"]
  J8 = female pin header, 8 pins [form="♀ (female)"]
  J9 = female pin header, 4 pins [form="♀ (female)"]
  J10 = female pin header, 8 pins [form="♀ (female)"]
  J11 = female pin header, 8 pins [form="♀ (female)"]
  J12 = female pin header, 4 pins [form="♀ (female)"]
  R5 = Resistor [tolerance=±5% resistance=220 package=THT]
  R6 = Resistor [tolerance=±5% resistance=220 package=THT]
  J59 = female pin header, 4 pins [form="♀ (female)"]
  J60 = longpad pin header, 1 pin [form="long pad"]
  J61 = longpad pin header, 1 pin [form="long pad"]
  J62 = longpad pin header, 1 pin [form="long pad"]
  J63 = longpad pin header, 1 pin [form="long pad"]
  J64 = longpad pin header, 1 pin [form="long pad"]
  J65 = longpad pin header, 1 pin [form="long pad"]
  R7 = Resistor [tolerance=±5% resistance=220 package=THT]
  R8 = Resistor [tolerance=±5% resistance=220 package=THT]
  J66 = female pin header, 4 pins [form="♀ (female)"]
  J67 = longpad pin header, 1 pin [form="long pad"]
  J68 = longpad pin header, 1 pin [form="long pad"]
  J69 = longpad pin header, 1 pin [form="long pad"]
  J70 = longpad pin header, 1 pin [form="long pad"]
  J71 = longpad pin header, 1 pin [form="long pad"]
  J72 = longpad pin header, 1 pin [form="long pad"]

nets:
  N1: J5.pin1, J8.pin1
  N2: J5.pin2, J8.pin2
  N3: J5.pin3, J8.pin3
  N4: J5.pin4, J8.pin4
  N5: J5.pin5, J8.pin5
  N6: J5.pin6, J8.pin6
  N7: J5.pin7, J8.pin7
  N8: J5.pin8, J8.pin8
  N9: J6.pin1, J7.pin1
  N10: J6.pin2, J7.pin2
  N11: J6.pin3, J7.pin3
  N12: J6.pin4, J7.pin4
  N13: J6.pin5, J7.pin5
  N14: J6.pin6, J7.pin6
  N15: J6.pin7, J7.pin7
  N16: J6.pin8, J7.pin8
  N17: J9.pin1, J12.pin1
  N18: J9.pin2, J12.pin2
  N19: J9.pin3, J12.pin3
  N20: J9.pin4, J12.pin4
  N21: J10.pin1, J11.pin1
  N22: J10.pin2, J11.pin2
  N23: J10.pin3, J11.pin3
  N24: J10.pin4, J11.pin4
  N25: J10.pin5, J11.pin5
  N26: J10.pin6, J11.pin6
  N27: J10.pin7, J11.pin7
  N28: J10.pin8, J11.pin8
  N29: R5.Pin_0, R6.Pin_0, J59.pin1, J64.pin1, J65.pin1
  N30: R5.Pin_1, J59.pin3, J62.pin1
  N31: R6.Pin_1, J59.pin4, J63.pin1
  N32: J59.pin2, J60.pin1, J61.pin1
  N33: R7.Pin_0, R8.Pin_0, J66.pin1, J71.pin1, J72.pin1
  N34: R7.Pin_1, J66.pin3, J69.pin1
  N35: R8.Pin_1, J66.pin4, J70.pin1
  N36: J66.pin2, J67.pin1, J68.pin1
