# Fritzing sketch Motherboard (saved by Fritzing 0.9.3b)
circuit board: 4.6cm x 6.3cm
circuit board: 3.56966cm x 1.28272cm
circuit board: 21cm x 14cm
circuit board: 4.6cm x 6.3cm

parts:
  J1 = female pin header, 1 pin [form="♀ (female)"]  # not connected
  J2 = female pin header, 1 pin [form="♀ (female)"]  # not connected
  J3 = female pin header, 1 pin [form="♀ (female)"]  # not connected
  J4 = female pin header, 1 pin [form="♀ (female)"]  # not connected
  J5 = female pin header, 8 pins [form="♀ (female)"]
  J6 = female pin header, 8 pins [form="♀ (female)"]
  J8 = female pin header, 2 pins [form="♀ (female)"]
  J11 = female pin header, 2 pins [form="♀ (female)"]
  J12 = female pin header, 2 pins [form="♀ (female)"]
  J13 = female pin header, 2 pins [form="♀ (female)"]
  J14 = female pin header, 2 pins [form="♀ (female)"]
  J15 = female pin header, 4 pins [form="♀ (female)"]
  J10 = female pin header, 2 pins [form="♀ (female)"]
  J18 = female pin header, 4 pins [form="♀ (female)"]
  J22 = female pin header, 8 pins [form="♀ (female)"]
  J23 = female pin header, 8 pins [form="♀ (female)"]
  J26 = double row female pin header, 6 pins [form="♀ (female)"]  # not connected
  J28 = female pin header, 10 pins [form="♀ (female)"]  # not connected
  J29 = female pin header, 8 pins [form="♀ (female)"]
  J30 = female pin header, 18 pins [form="♀ (female)"]
  J31 = female pin header, 18 pins [form="♀ (female)"]
  J36 = female pin header, 1 pin [form="♀ (female)"]  # not connected
  J38 = female pin header, 1 pin [form="♀ (female)"]  # not connected
  J39 = female pin header, 2 pins [form="♀ (female)"]
  J40 = female pin header, 4 pins [form="♀ (female)"]
  J17 = female pin header, 1 pin [form="♀ (female)"]  # not connected
  J16 = female pin header, 1 pin [form="♀ (female)"]  # not connected
  R22 = Resistor [tolerance=±5% resistance=220 package=THT]
  J62 = female pin header, 2 pins [form="♀ (female)"]
  J63 = female pin header, 4 pins [form="♀ (female)"]
  R27 = Resistor [tolerance=±5% resistance=220 package=THT]
  J67 = female pin header, 1 pin [form="♀ (female)"]  # not connected
  J68 = female pin header, 1 pin [form="♀ (female)"]  # not connected
  R28 = Resistor [tolerance=±5% resistance=220 package=THT]
  J69 = female pin header, 2 pins [form="♀ (female)"]
  J70 = female pin header, 2 pins [form="♀ (female)"]
  Q6 = NPN-Transistor [package="TO92 [THT]"]
  U7 = TLP621 [package=THT]
  R29 = Resistor [tolerance=±5% resistance=220 package=THT]
  R30 = Resistor [tolerance=±5% resistance=220 package=THT]
  J71 = female pin header, 2 pins [form="♀ (female)"]
  Q7 = NPN-Transistor [package="TO92 [THT]"]
  U8 = TLP621 [package=THT]
  R31 = Resistor [tolerance=±5% resistance=220 package=THT]
  R32 = Resistor [tolerance=±5% resistance=220 package=THT]
  Componente2 = Arduino Mega ADK (Rev3)  # not connected
  J7 = female pin header, 5 pins [form="♀ (female)"]
  Q8 = NPN-Transistor [package="TO92 [THT]"]
  R33 = Resistor [tolerance=±5% resistance=220 package=THT]
  J72 = female pin header, 2 pins [form="♀ (female)"]
  J73 = female pin header, 2 pins [form="♀ (female)"]
  J75 = female pin header, 2 pins [form="♀ (female)"]
  J76 = female pin header, 5 pins [form="♀ (female)"]
  J25 = female pin header, 6 pins [form="♀ (female)"]
  J32 = female pin header, 6 pins [form="♀ (female)"]
  J74 = female pin header, 2 pins [form="♀ (female)"]
  J77 = female pin header, 1 pin [form="♀ (female)"]  # not connected
  J78 = female pin header, 1 pin [form="♀ (female)"]  # not connected
  J79 = female pin header, 1 pin [form="♀ (female)"]  # not connected
  J80 = female pin header, 1 pin [form="♀ (female)"]  # not connected
  J81 = female pin header, 2 pins [form="♀ (female)"]
  J82 = female pin header, 2 pins [form="♀ (female)"]

nets:
  N1: J5.pin1, J22.pin6
  N2: J5.pin7, J6.pin7, J18.pin2, J30.pin1, J40.pin2, R22.Pin_0, J63.pin2, R28.Pin_0, U7.Pin_2, U8.Pin_2, J76.pin5, J81.pin1, J82.pin1
  N3: J6.pin1, J18.pin1, J30.pin18, J62.pin1, J63.pin1, J69.pin1, Q8.C, R33.Pin_0, J76.pin4, J81.pin2, J82.pin2
  N4: J6.pin2, R27.Pin_0
  N5: J6.pin3, J32.pin2
  N6: J6.pin8, J40.pin3
  N7: J8.pin1, J14.pin1, J73.pin2
  N8: J8.pin2, J13.pin2, J72.pin1
  N9: J11.pin2, J29.pin8, J40.pin4
  N10: J12.pin1, J29.pin7, J40.pin1
  N11: J15.pin1, J10.pin2, J70.pin1, U7.Pin_4, J71.pin1, U8.Pin_4, J7.pin5
  N12: J15.pin4, J10.pin1, Q6.E, Q7.E, J7.pin4
  N13: J18.pin3, J22.pin7
  N14: J18.pin4, J22.pin8
  N15: J23.pin2, Q8.B, R33.Pin_1
  N16: J23.pin3, R32.Pin_1
  N17: J23.pin4, R30.Pin_1
  N18: J23.pin8, R22.Pin_1, J62.pin2
  N19: J29.pin5, J7.pin1
  N20: J31.pin1, Q8.E
  N21: J39.pin1, J74.pin1
  N22: J39.pin2, J75.pin1
  N23: J63.pin3, J25.pin3
  N24: J63.pin4, J25.pin4
  N25: R27.Pin_1, J32.pin1
  N26: R28.Pin_1, J69.pin2, J32.pin4
  N27: J70.pin2, Q6.C
  N28: Q6.B, R29.Pin_0
  N29: U7.Pin_1, R30.Pin_0
  N30: U7.Pin_3, R29.Pin_1
  N31: J71.pin2, Q7.C
  N32: Q7.B, R31.Pin_0
  N33: U8.Pin_1, R32.Pin_0
  N34: U8.Pin_3, R31.Pin_1
  N35: J7.pin2, J25.pin2
  N36: J7.pin3, J25.pin1
  N37: J76.pin1, J25.pin5
  N38: J76.pin2, J25.pin6
  N39: J76.pin3, J32.pin3

notes:
  GND
  3V3
  Vin
  Clk
  MISO
  MOSI
  CS
  VBEN
  IRQ
  SD
  Created by
  5V
  IN2
  5V_ext
  IN3
  SG1
  5v
  SG2
  A0
  A1
  A2
  A3
  A5
  A4
  A6
  A8
  A9
  A10
  A11
  A12
  CREATED BY FEDERICO BOLELLI
  12 Vin
  OUT+
  OUT-
  IN+
  IN-
  220 Ω
  Amplificatore
  10 KΩ
  FEDERICO
  BOLELLI
  220 KΩ
  -5v EXT
  +5v EXT
  GND Arduino
  Segnale Arduino
  OPT
  SIG
  +5VE
  -5VE
  5V ARD
  BREW
  MATIC
  Stackable NOT to sold
  Male Header
  Stackable
  +
  -
  12V
  DFP
  (led)
  1K
  220
  SSR_1
  SSR_2
  10K
  DCDC
  down
  4K7
  5VA
  SIG1
  SIG2
  RELE
  DC DC
  BTN_1
  BTN_2
  LIGHT
  SW
  DT
  CLK
