# Fritzing sketch Motherboard (saved by Fritzing 0.9.3b)
circuit board: 21cm x 14cm
circuit board: 4.6cm x 6.3cm
circuit board: 1.28272cm x 3.56966cm

parts:
  J1 = female pin header, 1 pin [form="♀ (female)"]  # not connected
  J2 = female pin header, 1 pin [form="♀ (female)"]  # not connected
  J3 = female pin header, 1 pin [form="♀ (female)"]  # not connected
  J4 = female pin header, 1 pin [form="♀ (female)"]  # not connected
  J5 = female pin header, 8 pins [form="♀ (female)"]
  J6 = female pin header, 8 pins [form="♀ (female)"]
  J7 = female pin header, 4 pins [form="♀ (female)"]
  J8 = female pin header, 2 pins [form="♀ (female)"]
  J9 = female pin header, 2 pins [form="♀ (female)"]
  J11 = female pin header, 2 pins [form="♀ (female)"]
  J12 = female pin header, 2 pins [form="♀ (female)"]
  J13 = female pin header, 2 pins [form="♀ (female)"]
  J14 = female pin header, 2 pins [form="♀ (female)"]
  J15 = female pin header, 4 pins [form="♀ (female)"]
  J10 = female pin header, 2 pins [form="♀ (female)"]
  J18 = female pin header, 4 pins [form="♀ (female)"]
  J22 = female pin header, 8 pins [form="♀ (female)"]  # not connected
  J23 = female pin header, 8 pins [form="♀ (female)"]
  Componente1 = Arduino Mega ADK (Rev3)  # not connected
  J25 = female pin header, 8 pins [form="♀ (female)"]
  J24 = female pin header, 4 pins [form="♀ (female)"]  # not connected
  Componente2 = Arduino Mega ADK (Rev3)
  J26 = double row female pin header, 6 pins [form="♀ (female)"]  # not connected
  J28 = female pin header, 10 pins [form="♀ (female)"]  # not connected
  J29 = female pin header, 8 pins [form="♀ (female)"]  # not connected
  J30 = female pin header, 18 pins [form="♀ (female)"]
  J31 = female pin header, 18 pins [form="♀ (female)"]  # not connected
  J32 = female pin header, 4 pins [form="♀ (female)"]  # not connected
  U4 = TLP621 [package=THT]
  Q4 = NPN-Transistor [package="TO92 [THT]"]
  R6 = Resistor [tolerance=±5% resistance=220 package=THT]
  R9 = Resistor [tolerance=±5% resistance=220 package=THT]
  J36 = female pin header, 1 pin [form="♀ (female)"]  # not connected
  J37 = female pin header, 1 pin [form="♀ (female)"]  # not connected
  J38 = female pin header, 1 pin [form="♀ (female)"]  # not connected
  J39 = female pin header, 2 pins [form="♀ (female)"]
  J40 = female pin header, 4 pins [form="♀ (female)"]
  J17 = female pin header, 1 pin [form="♀ (female)"]  # not connected
  J16 = female pin header, 1 pin [form="♀ (female)"]  # not connected
  R22 = Resistor [tolerance=±5% resistance=220 package=THT]
  J62 = female pin header, 2 pins [form="♀ (female)"]
  J63 = female pin header, 4 pins [form="♀ (female)"]
  J35 = female pin header, 2 pins [form="♀ (female)"]
  J64 = female pin header, 2 pins [form="♀ (female)"]
  Q5 = NPN-Transistor [package="TO92 [THT]"]
  U6 = TLP621 [package=THT]
  R25 = Resistor [tolerance=±5% resistance=220 package=THT]
  R26 = Resistor [tolerance=±5% resistance=220 package=THT]
  R27 = Resistor [tolerance=±5% resistance=220 package=THT]
  J65 = female pin header, 2 pins [form="♀ (female)"]
  J66 = female pin header, 2 pins [form="♀ (female)"]

nets:
  N1: J5.pin7, J6.pin7, J18.pin2, J30.pin1, J40.pin2, R22.Pin_0, J63.pin2, J65.pin1, J66.pin1
  N2: J6.pin1, J18.pin1, J30.pin18, J62.pin1, J63.pin1, J65.pin2, J66.pin2
  N3: J6.pin2, R27.Pin_0
  N4: J6.pin3, Componente2.D17/RX2
  N5: J6.pin8, J40.pin3
  N6: J7.pin1, J15.pin1, J10.pin2, J39.pin1
  N7: J7.pin2, J25.pin2
  N8: J7.pin3, J25.pin1
  N9: J7.pin4, J15.pin4, J10.pin1, J39.pin2
  N10: J8.pin1, J14.pin1
  N11: J8.pin2, J13.pin2
  N12: J9.pin1, J12.pin1, J40.pin1
  N13: J9.pin2, J11.pin2, J40.pin4
  N14: J18.pin3, J25.pin5
  N15: J18.pin4, J25.pin6
  N16: J23.pin8, R22.Pin_1, J62.pin2
  N17: J25.pin3, J63.pin3
  N18: J25.pin4, J63.pin4
  N19: Componente2.D16/TX2, R27.Pin_1
  N20: U4.Pin_1, R9.Pin_1
  N21: U4.Pin_4, J35.pin2
  N22: U4.Pin_3, R6.Pin_0
  N23: Q4.B, R6.Pin_1
  N24: Q4.C, J35.pin1
  N25: J64.pin1, U6.Pin_4
  N26: J64.pin2, Q5.C
  N27: Q5.B, R26.Pin_0
  N28: U6.Pin_1, R25.Pin_0
  N29: U6.Pin_3, R26.Pin_1

notes:
  GND
  3V3
  Vin
  Clk
  MISO
  MOSI
  CS
  VBEN
  IRQ
  Relé Module
  SD
  DCDC
  Step
  Down
  Created by
  5V
  IN2
  5V_ext
  IN3
  SG1
  5v
  SG2
  A0
  A1
  A2
  A3
  A5
  A4
  A6
  A8
  A9
  A15
  A12
  A10
  A11
  A14
  7
  6
  1
  3
  16
  17
  14
  2
  0
  15
  CREATED BY FEDERICO BOLELLI
  IN1
  12V in
  12 Vin
  5V in
  The Available Pins
  Are Labeled
  7V out
  DFPlayer
  OUT+
  OUT-
  IN+
  IN-
  OPT
  220 Ω
  Segnale Arduino
  GND Arduino
  +5v EXT
  -5v EXT
  RX
  TX
  SPK_1
  SPK_2
  SD in
  LED
  Amplificatore
  10 KΩ
  220 KΩ
  4
  5
  FEDERICO
  BOLELLI
  GND External
  6-12 External
  KΩ
