# Fritzing sketch XLS Single (saved by Fritzing 0.9.3b)
circuit board: 2.18107cm x 1.58857cm

parts:
  R2 = Resistor [tolerance=±5% resistance=220 package=THT]
  J51 = longpad pin header, 1 pin [form="long pad"]
  J49 = longpad pin header, 1 pin [form="long pad"]
  J50 = longpad pin header, 1 pin [form="long pad"]
  J48 = female pin header, 3 pins [form="♀ (female)"]

nets:
  N1: R2.Pin_0, J51.pin1, J48.pin1
  N2: R2.Pin_1, J50.pin1, J48.pin3
  N3: J49.pin1, J48.pin2

notes:
  GND
  3V3
  Vin
  Clk
  MISO
  MOSI
  CS
  VBEN
  IRQ
